// Digital circuit Digital_Design.dig as structural Verilog
module Digital_Design (
);

  wire add_1_c_o, add_1_s, and_1_out, and_2_out, and_3_out, and_4_out, and_5_out, button_1_out, button_2_out,
       button_3_out, button_4_out, button_5_out, button_6_out, button_7_out, button_8_out, Clk_2_out,
       Clk_3_out, Clk_4_out, Clk_5_out, Clk_6_out, Clk_7_out, Clk_8_out, Clk_9_out, Clk_10_out, Clk_11_out,
       Clk_12_out, Clk_13_out, Clk_14_out, Clk_15_out, Clk_16_out, Clk_17_out, Clk_18_out, Clk_19_out,
       Clk_20_out, Clk_out, D_2_out, D_3_out, D_4_out, D_5_out, D_6_out, D_7_out, D_8_out, d_ff_1_nq,
       d_ff_1_q, d_ff_2_nq, d_ff_2_q, d_ff_3_nq, d_ff_3_q, d_ff_4_q, d_ff_5_q, d_ff_6_q, d_ff_7_q, d_ff_8_q,
       d_ff_as_1_nq, d_ff_as_1_q, d_ff_as_2_nq, d_ff_as_2_q, d_ff_as_3_nq, d_ff_as_3_q, d_ff_as_4_nq,
       d_ff_as_4_q, d_ff_as_5_nq, d_ff_as_5_q, d_ff_as_6_q, d_ff_as_7_q, d_ff_as_8_q, d_ff_as_9_nq,
       d_ff_as_9_q, d_ff_as_10_nq, D_out, En_2_out, En_out, J_2_out, J_3_out, J_4_out, J_5_out, J_out,
       jk_ff_1_nq, jk_ff_1_q, jk_ff_2_nq, jk_ff_2_q, jk_ff_3_nq, jk_ff_3_q, K_2_out, K_3_out, K_4_out,
       K_5_out, K_out, nand_1_out, nand_2_out, nand_3_out, nand_4_out, nand_5_out, nand_6_out, nand_7_out,
       nand_8_out, nand_9_out, nand_10_out, nand_11_out, nand_12_out, nand_13_out, nand_14_out, nand_15_out,
       nand_16_out, nand_17_out, nand_18_out, nand_19_out, nand_20_out, nand_21_out, nand_22_out,
       nand_23_out, nand_24_out, nand_25_out, nand_26_out, nand_27_out, nand_28_out, nand_29_out,
       nand_30_out, nand_31_out, nand_32_out, nand_33_out, nand_34_out, nand_35_out, nand_36_out,
       nand_37_out, nand_38_out, nand_39_out, nand_40_out, nand_41_out, nand_42_out, nand_43_out,
       nand_44_out, nand_45_out, nand_46_out, nand_47_out, nand_48_out, nand_49_out, nand_50_out,
       nand_51_out, nand_52_out, nand_53_out, nand_54_out, nand_55_out, nand_56_out, nand_57_out,
       nand_58_out, nand_59_out, nand_60_out, nand_61_out, nand_62_out, nand_63_out, nand_64_out,
       nand_65_out, nand_66_out, nor_1_out, nor_2_out, not_1_out, not_2_out, not_3_out, not_4_out, not_5_out,
       not_6_out, not_7_out, not_8_out, not_9_out, not_10_out, not_11_out, not_12_out, not_13_out,
       not_14_out, nR_out, nS_out, or_1_out, or_2_out, R_2_out, R_out, Reset_2_out, Reset_3_out, Reset_4_out,
       Reset_out, S_2_out, S_out, T_2_out, T_3_out, T_4_out, T_5_out, T_6_out, t_ff_1_nq, t_ff_1_q, T_out,
       xor_1_out, xor_2_out;

  nor nor_1 (nor_1_out, nor_2_out, S_out);
  DipSwitch S (.out(S_out));
  DipSwitch R (.out(R_out));
  DipSwitch nS (.out(nS_out));
  DipSwitch nR (.out(nR_out));
  nand nand_1 (nand_1_out, nS_out, nand_2_out);
  nand nand_2 (nand_2_out, nand_1_out, nR_out);
  nor nor_2 (nor_2_out, nor_1_out, R_out);
  LED Q (.in(nand_1_out));
  LED nQ (.in(nand_2_out));
  LED nQ_2 (.in(nor_1_out));
  LED Q_2 (.in(nor_2_out));
  DipSwitch S_2 (.out(S_2_out));
  DipSwitch En (.out(En_out));
  DipSwitch R_2 (.out(R_2_out));
  DipSwitch D (.out(D_out));
  DipSwitch En_2 (.out(En_2_out));
  not not_1 (not_1_out, D_out);
  nand nand_3 (nand_3_out, S_2_out, En_out);
  nand nand_4 (nand_4_out, En_out, R_2_out);
  nand nand_5 (nand_5_out, D_out, En_2_out);
  nand nand_6 (nand_6_out, En_2_out, not_1_out);
  nand nand_7 (nand_7_out, nand_3_out, nand_8_out);
  nand nand_8 (nand_8_out, nand_7_out, nand_4_out);
  nand nand_9 (nand_9_out, nand_5_out, nand_10_out);
  nand nand_10 (nand_10_out, nand_9_out, nand_6_out);
  LED Q_3 (.in(nand_7_out));
  LED nQ_3 (.in(nand_8_out));
  LED Q_4 (.in(nand_9_out));
  LED nQ_4 (.in(nand_10_out));
  DipSwitch D_2 (.out(D_2_out));
  DipSwitch Clk (.out(Clk_out));
  DipSwitch Clk_2 (.out(Clk_2_out));
  DipSwitch D_3 (.out(D_3_out));
  DipSwitch Clk_3 (.out(Clk_3_out));
  DipSwitch D_4 (.out(D_4_out));
  DipSwitch Reset (.out(Reset_out));
  nand nand_11 (nand_11_out, D_2_out, Clk_out);
  nand nand_12 (nand_12_out, Clk_out, not_2_out);
  not not_2 (not_2_out, D_2_out);
  nand nand_13 (nand_13_out, nand_16_out, nand_14_out);
  nand nand_14 (nand_14_out, nand_13_out, Clk_2_out);
  nand nand_15 (nand_15_out, nand_14_out, Clk_2_out, nand_16_out);
  nand nand_16 (nand_16_out, nand_15_out, D_3_out);
  nand nand_17 (nand_17_out, nand_11_out, nand_18_out);
  nand nand_18 (nand_18_out, nand_17_out, nand_12_out);
  not not_3 (not_3_out, Clk_out);
  nand nand_19 (nand_19_out, nand_22_out, nand_20_out);
  nand nand_20 (nand_20_out, nand_19_out, Reset_out, Clk_3_out);
  nand nand_21 (nand_21_out, nand_20_out, Clk_3_out, nand_22_out);
  nand nand_22 (nand_22_out, nand_21_out, Reset_out, D_4_out);
  nand nand_23 (nand_23_out, nand_17_out, not_3_out);
  nand nand_24 (nand_24_out, not_3_out, not_4_out);
  not not_4 (not_4_out, nand_17_out);
  nand nand_25 (nand_25_out, nand_14_out, nand_26_out);
  nand nand_26 (nand_26_out, nand_25_out, nand_15_out);
  nand nand_27 (nand_27_out, nand_23_out, nand_28_out);
  nand nand_28 (nand_28_out, nand_27_out, nand_24_out);
  LED Q_5 (.in(nand_25_out));
  LED nQ_5 (.in(nand_26_out));
  nand nand_29 (nand_29_out, nand_20_out, nand_30_out);
  nand nand_30 (nand_30_out, nand_29_out, Reset_out, nand_21_out);
  LED Q_6 (.in(nand_27_out));
  LED nQ_6 (.in(nand_28_out));
  LED Q_7 (.in(nand_29_out));
  LED nQ_7 (.in(nand_30_out));
  DipSwitch D_5 (.out(D_5_out));
  DipSwitch Clk_4 (.out(Clk_4_out));
  D_FF d_ff_1 (.D(D_5_out), .C(Clk_4_out), .Q(d_ff_1_q), .nQ(d_ff_1_nq));
  DipSwitch D_6 (.out(D_6_out));
  DipSwitch Clk_5 (.out(Clk_5_out));
  D_FF d_ff_2 (.D(D_6_out), .C(~Clk_5_out), .Q(d_ff_2_q), .nQ(d_ff_2_nq));
  LED Q_8 (.in(d_ff_1_q));
  LED nQ_8 (.in(d_ff_1_nq));
  LED Q_9 (.in(d_ff_2_q));
  LED nQ_9 (.in(d_ff_2_nq));
  DipSwitch D_7 (.out(D_7_out));
  DipSwitch Clk_6 (.out(Clk_6_out));
  DipSwitch Reset_2 (.out(Reset_2_out));
  D_FF_AS d_ff_as_1 (.Set(1'b0), .D(D_7_out), .C(Clk_6_out), .Clr(Reset_2_out), .Q(d_ff_as_1_q), .nQ(d_ff_as_1_nq));
  LED Q_10 (.in(d_ff_as_1_q));
  LED nQ_10 (.in(d_ff_as_1_nq));
  DipSwitch J (.out(J_out));
  DipSwitch Clk_7 (.out(Clk_7_out));
  DipSwitch K (.out(K_out));
  DipSwitch Clk_8 (.out(Clk_8_out));
  DipSwitch J_2 (.out(J_2_out));
  DipSwitch K_2 (.out(K_2_out));
  not not_5 (not_5_out, K_2_out);
  and and_1 (and_1_out, J_2_out, nand_44_out);
  and and_2 (and_2_out, not_5_out, nand_43_out);
  nand nand_31 (nand_31_out, nand_42_out, J_out, Clk_7_out);
  nand nand_32 (nand_32_out, Clk_7_out, K_out, nand_41_out);
  nand nand_33 (nand_33_out, nand_31_out, nand_34_out);
  nand nand_34 (nand_34_out, nand_33_out, nand_32_out);
  not not_6 (not_6_out, Clk_7_out);
  or or_1 (or_1_out, and_1_out, and_2_out);
  not not_7 (not_7_out, nand_33_out);
  nand nand_35 (nand_35_out, nand_33_out, not_6_out);
  nand nand_36 (nand_36_out, not_6_out, not_7_out);
  nand nand_37 (nand_37_out, nand_40_out, nand_38_out);
  nand nand_38 (nand_38_out, nand_37_out, Clk_8_out);
  nand nand_39 (nand_39_out, nand_38_out, Clk_8_out, nand_40_out);
  nand nand_40 (nand_40_out, nand_39_out, or_1_out);
  nand nand_41 (nand_41_out, nand_35_out, nand_42_out);
  nand nand_42 (nand_42_out, nand_41_out, nand_36_out);
  LED Q_11 (.in(nand_41_out));
  LED nQ_11 (.in(nand_42_out));
  nand nand_43 (nand_43_out, nand_38_out, nand_44_out);
  nand nand_44 (nand_44_out, nand_43_out, nand_39_out);
  LED Q_12 (.in(nand_43_out));
  LED nQ_12 (.in(nand_44_out));
  DipSwitch J_3 (.out(J_3_out));
  DipSwitch Clk_9 (.out(Clk_9_out));
  DipSwitch K_3 (.out(K_3_out));
  JK_FF jk_ff_1 (.J(J_3_out), .C(~Clk_9_out), .K(K_3_out), .Q(jk_ff_1_q), .nQ(jk_ff_1_nq));
  LED Q_13 (.in(jk_ff_1_q));
  LED nQ_13 (.in(jk_ff_1_nq));
  DipSwitch J_4 (.out(J_4_out));
  JK_FF jk_ff_2 (.J(J_4_out), .C(Clk_10_out), .K(K_4_out), .Q(jk_ff_2_q), .nQ(jk_ff_2_nq));
  DipSwitch Clk_10 (.out(Clk_10_out));
  DipSwitch K_4 (.out(K_4_out));
  DipSwitch J_5 (.out(J_5_out));
  DipSwitch K_5 (.out(K_5_out));
  not not_8 (not_8_out, K_5_out);
  DipSwitch Clk_11 (.out(Clk_11_out));
  and and_3 (and_3_out, d_ff_3_nq, J_5_out);
  and and_4 (and_4_out, not_8_out, d_ff_3_q);
  LED Q_14 (.in(jk_ff_2_q));
  LED nQ_14 (.in(jk_ff_2_nq));
  or or_2 (or_2_out, and_3_out, and_4_out);
  D_FF d_ff_3 (.D(or_2_out), .C(Clk_11_out), .Q(d_ff_3_q), .nQ(d_ff_3_nq));
  DipSwitch Clk_12 (.out(Clk_12_out));
  and and_5 (and_5_out, Clk_12_out, T_out);
  DipSwitch T (.out(T_out));
  DipSwitch Clk_13 (.out(Clk_13_out));
  DipSwitch T_2 (.out(T_2_out));
  DipSwitch Clk_14 (.out(Clk_14_out));
  DipSwitch T_3 (.out(T_3_out));
  xor xor_1 (xor_1_out, T_2_out, nand_61_out);
  nand nand_45 (nand_45_out, nand_66_out, T_3_out, Clk_14_out);
  nand nand_46 (nand_46_out, Clk_14_out, T_3_out, nand_65_out);
  nand nand_47 (nand_47_out, nand_64_out, and_5_out);
  nand nand_48 (nand_48_out, and_5_out, nand_63_out);
  not not_9 (not_9_out, Clk_14_out);
  nand nand_49 (nand_49_out, nand_47_out, nand_50_out);
  nand nand_50 (nand_50_out, nand_49_out, nand_48_out);
  not not_10 (not_10_out, and_5_out);
  nand nand_51 (nand_51_out, nand_54_out, nand_52_out);
  nand nand_52 (nand_52_out, nand_51_out, Clk_13_out);
  nand nand_53 (nand_53_out, nand_52_out, Clk_13_out, nand_54_out);
  nand nand_54 (nand_54_out, nand_53_out, xor_1_out);
  nand nand_55 (nand_55_out, nand_45_out, nand_56_out);
  nand nand_56 (nand_56_out, nand_55_out, nand_46_out);
  not not_11 (not_11_out, nand_55_out);
  not not_12 (not_12_out, nand_49_out);
  nand nand_57 (nand_57_out, nand_55_out, not_9_out);
  nand nand_58 (nand_58_out, not_9_out, not_11_out);
  nand nand_59 (nand_59_out, nand_49_out, not_10_out);
  nand nand_60 (nand_60_out, not_10_out, not_12_out);
  nand nand_61 (nand_61_out, nand_52_out, nand_62_out);
  nand nand_62 (nand_62_out, nand_61_out, nand_53_out);
  nand nand_63 (nand_63_out, nand_59_out, nand_64_out);
  nand nand_64 (nand_64_out, nand_63_out, nand_60_out);
  nand nand_65 (nand_65_out, nand_57_out, nand_66_out);
  nand nand_66 (nand_66_out, nand_65_out, nand_58_out);
  LED Q_15 (.in(nand_61_out));
  LED nQ_15 (.in(nand_62_out));
  LED Q_16 (.in(nand_65_out));
  LED nQ_16 (.in(nand_66_out));
  LED Q_17 (.in(nand_63_out));
  LED nQ_17 (.in(nand_64_out));
  DipSwitch Clk_15 (.out(Clk_15_out));
  DipSwitch T_4 (.out(T_4_out));
  xor xor_2 (xor_2_out, d_ff_4_q, T_5_out);
  DipSwitch T_5 (.out(T_5_out));
  DipSwitch Clk_16 (.out(Clk_16_out));
  DipSwitch T_6 (.out(T_6_out));
  DipSwitch Clk_17 (.out(Clk_17_out));
  JK_FF jk_ff_3 (.J(T_4_out), .C(~Clk_15_out), .K(T_4_out), .Q(jk_ff_3_q), .nQ(jk_ff_3_nq));
  T_FF t_ff_1 (.T(T_6_out), .C(Clk_17_out), .Q(t_ff_1_q), .nQ(t_ff_1_nq));
  D_FF d_ff_4 (.D(xor_2_out), .C(Clk_16_out), .Q(d_ff_4_q));  // open: nQ
  LED Q_18 (.in(t_ff_1_q));
  LED nQ_18 (.in(t_ff_1_nq));
  LED Q_19 (.in(jk_ff_3_q));
  LED nQ_19 (.in(jk_ff_3_nq));
  D_FF d_ff_5 (.D(D_8_out), .C(Clk_18_out), .Q(d_ff_5_q));  // open: nQ
  DipSwitch D_8 (.out(D_8_out));
  DipSwitch Clk_18 (.out(Clk_18_out));
  DipSwitch Clk_19 (.out(Clk_19_out));
  DipSwitch Reset_3 (.out(Reset_3_out));
  LED led_1 (.in(d_ff_5_q));
  not not_13 (not_13_out, Clk_19_out);
  D_FF d_ff_6 (.D(d_ff_5_q), .C(Clk_18_out), .Q(d_ff_6_q));  // open: nQ
  D_FF_AS d_ff_as_2 (
    .Set(1'b0), .D(d_ff_as_2_nq), .C(not_13_out), .Clr(Reset_3_out), .Q(d_ff_as_2_q), .nQ(d_ff_as_2_nq));
  D_FF_AS d_ff_as_3 (
    .Set(1'b0), .D(d_ff_as_3_nq), .C(d_ff_as_2_nq), .Clr(Reset_3_out), .Q(d_ff_as_3_q), .nQ(d_ff_as_3_nq));
  D_FF_AS d_ff_as_4 (
    .Set(1'b0), .D(d_ff_as_4_nq), .C(d_ff_as_3_nq), .Clr(Reset_3_out), .Q(d_ff_as_4_q), .nQ(d_ff_as_4_nq));
  D_FF_AS d_ff_as_5 (
    .Set(1'b0), .D(d_ff_as_5_nq), .C(d_ff_as_4_nq), .Clr(Reset_3_out), .Q(d_ff_as_5_q), .nQ(d_ff_as_5_nq));
  LED led_2 (.in(d_ff_6_q));
  D_FF d_ff_7 (.D(d_ff_6_q), .C(Clk_18_out), .Q(d_ff_7_q));  // open: nQ
  LED Q_0 (.in(d_ff_as_2_q));
  LED Q_1 (.in(d_ff_as_3_q));
  LED Q_2_dup2 (.in(d_ff_as_4_q));
  LED Q_3_dup2 (.in(d_ff_as_5_q));
  LED led_3 (.in(d_ff_7_q));
  D_FF d_ff_8 (.D(d_ff_7_q), .C(Clk_18_out), .Q(d_ff_8_q));  // open: nQ
  LED led_4 (.in(d_ff_8_q));
  Button button_1 (.out(button_1_out));
  Button button_2 (.out(button_2_out));
  D_FF_AS d_ff_as_6 (.Set(button_1_out), .D(add_1_s), .C(Clk_20_out), .Clr(button_2_out), .Q(d_ff_as_6_q));  // open: nQ
  LED led_5 (.in(d_ff_as_6_q));
  D_FF_AS d_ff_as_7 (
    .Set(button_3_out), .D(d_ff_as_6_q), .C(Clk_20_out), .Clr(button_4_out), .Q(d_ff_as_7_q));  // open: nQ
  Button button_3 (.out(button_3_out));
  Button button_4 (.out(button_4_out));
  LED led_6 (.in(d_ff_as_7_q));
  D_FF_AS d_ff_as_8 (
    .Set(button_5_out), .D(d_ff_as_7_q), .C(Clk_20_out), .Clr(button_6_out), .Q(d_ff_as_8_q));  // open: nQ
  Button button_5 (.out(button_5_out));
  Button button_6 (.out(button_6_out));
  LED led_7 (.in(d_ff_as_8_q));
  Button button_7 (.out(button_7_out));
  Button button_8 (.out(button_8_out));
  D_FF_AS d_ff_as_9 (
    .Set(button_7_out), .D(d_ff_as_8_q), .C(Clk_20_out), .Clr(button_8_out), .Q(d_ff_as_9_q),
    .nQ(d_ff_as_9_nq));
  LED led_8 (.in(d_ff_as_9_q));
  DipSwitch Clk_20 (.out(Clk_20_out));
  Button Reset_4 (.out(Reset_4_out));
  not not_14 (not_14_out, add_1_c_o);
  Add add_1 (.a(d_ff_as_9_nq), .b(d_ff_as_10_nq), .c_i(1'b0), .s(add_1_s), .c_o(add_1_c_o));
  D_FF_AS d_ff_as_10 (.Set(1'b0), .D(not_14_out), .C(Clk_20_out), .Clr(Reset_4_out), .nQ(d_ff_as_10_nq));  // open: Q
  LED led_9 (.in(add_1_s));

  // Notes on the sheet:
  //   SR Latch
  //   ~SR Latch
  //   Control SR Latch
  //   D Latch
  //   D Flip-Flop (Master-Slave, Faling Edge)
  //   D Flip-Flop (Rising Edge)
  //   Async D Flip-Flop (Rising Edge)
  //   D
  //   En
  //   ~S
  //   ~R
  //   Clk
  //   Q
  //   ~Q
  //   JK Flip-Flop (Master-Slave, Faling Edge)
  //   JK Flip-Flop (Rising Edge)
  //   T Flip-Flop (Master-Slave, Faling Edge)
  //   T Flip-Flop (Rising Edge)
  //   J
  //   K
  //   Shift Register
endmodule
